# Fritzing sketch hat (saved by Fritzing 0.9.4)
breadboards: 1

parts:
  ULN1 = Darlington Driver [package=so018]
  ULN2 = Darlington Driver [package=so018]
  LED1 = LED - 5mm [color="Red (633nm)" package="5 mm [THT]"]
  LED2 = LED - 5mm [color="Orange (612nm)" package="5 mm [THT]"]
  LED3 = LED - 5mm [color="Yellow (595nm)" package="5 mm [THT]"]
  LED4 = LED - 5mm [color="Green (565nm)" package="5 mm [THT]"]
  LED5 = LED - 5mm [color="Blue (505nm)" package="5 mm [THT]"]
  LED6 = RGB LED - (4 legs) [package="5 mm [THT]"]
  LED7 = RGB LED - (4 legs) [package="5 mm [THT]"]
  BUZZER = Buzzer 12mm [package=buzzer-ccv-kit]
  R1 = Resistor [tolerance=±5% resistance=330 package=THT]
  R2 = Resistor [tolerance=±5% resistance=330 package=THT]
  R3 = Resistor [tolerance=±5% resistance=330 package=THT]
  R4 = Resistor [tolerance=±5% resistance=330 package=THT]
  R5 = Resistor [tolerance=±5% resistance=330 package=THT]
  R7 = Resistor [tolerance=±5% resistance=750 package=THT]
  R8 = Resistor [tolerance=±5% resistance=750 package=THT]
  R9 = Resistor [tolerance=±5% resistance=750 package=THT]
  R10 = Resistor [tolerance=±5% resistance=750 package=THT]
  R11 = Resistor [tolerance=±5% resistance=750 package=THT]
  R6 = Resistor [tolerance=±5% resistance=750 package=THT]
  TILT1 = Tilt Switch [package=THT]
  TILT2 = Tilt Switch [package=THT]
  B1 = SWITCH-MOMENTARY-2 [package=tactile-pth]
  B2 = SWITCH-MOMENTARY-2 [package=tactile-pth]
  B3 = SWITCH-MOMENTARY-2 [package=tactile-pth]
  POT = SLIDER [package=slider]
  LDR = Photocell (LDR) [package=THT]
  C1 = Electrolytic Capacitor [capacitance=1µF package="100 mil [THT, electrolytic]"]
  C2 = Tantalum Capacitor [capacitance=100nF package="A 3216 [SMD, tantalum]"]
  R13 = Resistor [tolerance=±5% resistance=1k package=THT]
  R14 = Resistor [tolerance=±5% resistance=330 package=THT]
  SW1 = DIP SWITCH [package=dipswitch-02]
  SW2 = DIP SWITCH [package=dipswitch-02]
  J3 = single row smd male pin header, 2 pins [form="♂ (male)"]
  J2 = single row smd male pin header, 2 pins [form="♂ (male)"]
  J1 = single row smd male pin header, 2 pins [form="♂ (male)"]
  O1 = male pin header, 1 pin [form="♂ (male)"]
  O2 = male pin header, 1 pin [form="♂ (male)"]
  O3 = male pin header, 1 pin [form="♂ (male)"]
  O4 = male pin header, 1 pin [form="♂ (male)"]
  3v3_|_1 = male pin header, 1 pin [form="♂ (male)"]
  2_|_5V = male pin header, 1 pin [form="♂ (male)"]
  GPIO_2_|_3 = male pin header, 1 pin [form="♂ (male)"]
  4_|_5V = male pin header, 1 pin [form="♂ (male)"]
  GPIO_3_|_5 = male pin header, 1 pin [form="♂ (male)"]
  6_|_GND = male pin header, 1 pin [form="♂ (male)"]
  GPIO_4_|_7 = male pin header, 1 pin [form="♂ (male)"]
  8_|_GPIO_14 = male pin header, 1 pin [form="♂ (male)"]
  GND_|_9 = male pin header, 1 pin [form="♂ (male)"]
  10_|_GPIO_15 = male pin header, 1 pin [form="♂ (male)"]
  GPIO_17_|_11 = male pin header, 1 pin [form="♂ (male)"]
  12_|_GPIO_18 = male pin header, 1 pin [form="♂ (male)"]
  GPIO_27_|_13 = male pin header, 1 pin [form="♂ (male)"]
  14_|_GND = male pin header, 1 pin [form="♂ (male)"]
  GPIO_22_|_15 = male pin header, 1 pin [form="♂ (male)"]
  16_|_GPIO_23 = male pin header, 1 pin [form="♂ (male)"]
  3v3_|_17 = male pin header, 1 pin [form="♂ (male)"]
  20_|_GND = male pin header, 1 pin [form="♂ (male)"]
  GPIO_10_|_19 = male pin header, 1 pin [form="♂ (male)"]
  22_|_GPIO_25 = male pin header, 1 pin [form="♂ (male)"]
  GND_|_25 = male pin header, 1 pin [form="♂ (male)"]
  38_|_GPIO_20 = male pin header, 1 pin [form="♂ (male)"]
  26_|_GPIO_7 = male pin header, 1 pin [form="♂ (male)"]
  GPIO_0_|_27 = male pin header, 1 pin [form="♂ (male)"]  # not connected
  GPIO_11_|_23 = male pin header, 1 pin [form="♂ (male)"]
  GPIO_9_|_21 = male pin header, 1 pin [form="♂ (male)"]
  40_|_GPIO_21 = male pin header, 1 pin [form="♂ (male)"]
  GPIO_13_|_33 = male pin header, 1 pin [form="♂ (male)"]
  GND_|_39 = male pin header, 1 pin [form="♂ (male)"]
  24_|_GPIO_8 = male pin header, 1 pin [form="♂ (male)"]
  GPIO_26_|_37 = male pin header, 1 pin [form="♂ (male)"]
  34_|_GND = male pin header, 1 pin [form="♂ (male)"]
  28_|_GPIO_1 = male pin header, 1 pin [form="♂ (male)"]  # not connected
  GPIO_6_|_31 = male pin header, 1 pin [form="♂ (male)"]
  18_|_GPIO_24 = male pin header, 1 pin [form="♂ (male)"]
  32_|_GPIO_12 = male pin header, 1 pin [form="♂ (male)"]
  GPIO_19_|_35 = male pin header, 1 pin [form="♂ (male)"]
  30_|_GND = male pin header, 1 pin [form="♂ (male)"]
  36_|_GPIO_16 = male pin header, 1 pin [form="♂ (male)"]
  GPIO_5_|_29 = male pin header, 1 pin [form="♂ (male)"]

nets:
  N1: ULN1.1, R13.Pin_1, GPIO_3_|_5.pin1
  N2: ULN1.2, 8_|_GPIO_14.pin1
  N3: ULN1.3, 10_|_GPIO_15.pin1
  N4: ULN1.4, 12_|_GPIO_18.pin1
  N5: ULN1.5, GPIO_2_|_3.pin1
  N6: ULN1.6, 16_|_GPIO_23.pin1
  N7: ULN1.7, 18_|_GPIO_24.pin1
  N8: ULN1.8, GPIO_19_|_35.pin1
  GND: ULN1.9, ULN2.9, TILT2.Pin_1, B1.1, B2.1, B3.1, C1.-, C2.-, R13.Pin_0, SW1.3, SW1.4, SW2.3, J3.pin1, J3.pin2, 6_|_GND.pin1, GND_|_9.pin1, 14_|_GND.pin1, 20_|_GND.pin1, GND_|_25.pin1, GND_|_39.pin1, 34_|_GND.pin1, 30_|_GND.pin1
  N9: ULN1.11, LED4.cathode
  N10: ULN1.12, O3.pin1
  N11: ULN1.13, LED3.cathode
  N12: ULN1.14, O2.pin1
  N13: ULN1.15, LED2.cathode
  N14: ULN1.16, O1.pin1
  N15: ULN1.17, LED1.cathode
  N16: ULN1.18, BUZZER.1
  N17: ULN2.1, 24_|_GPIO_8.pin1
  N18: ULN2.2, 26_|_GPIO_7.pin1
  N19: ULN2.3, 22_|_GPIO_25.pin1
  N20: ULN2.4, GPIO_26_|_37.pin1
  N21: ULN2.5, 32_|_GPIO_12.pin1
  N22: ULN2.6, 40_|_GPIO_21.pin1
  N23: ULN2.7, 36_|_GPIO_16.pin1
  N24: ULN2.8, 38_|_GPIO_20.pin1
  N25: ULN2.11, R9.Pin_0
  N26: ULN2.12, R11.Pin_0
  N27: ULN2.13, R10.Pin_0
  N28: ULN2.14, R6.Pin_0
  N29: ULN2.15, R8.Pin_0
  N30: ULN2.16, R7.Pin_0
  N31: ULN2.17, O4.pin1
  N32: ULN2.18, LED5.cathode
  N33: LED1.anode, R1.Pin_0
  N34: LED2.anode, R2.Pin_0
  N35: LED3.anode, R3.Pin_0
  N36: LED4.anode, R4.Pin_0
  N37: LED5.anode, R5.Pin_0
  N38: LED6.red_cathode, R6.Pin_1
  5V: LED6.common_anode, LED7.common_anode, R1.Pin_1, R2.Pin_1, R3.Pin_1, R4.Pin_1, R5.Pin_1, J2.pin2, J1.pin1, J1.pin2, 2_|_5V.pin1, 4_|_5V.pin1
  N39: LED6.green_cathode, R7.Pin_1
  N40: LED6.blue_cathode, R8.Pin_1
  N41: LED7.red_cathode, R9.Pin_1
  N42: LED7.green_cathode, R10.Pin_1
  N43: LED7.blue_cathode, R11.Pin_1
  N44: BUZZER.2, J2.pin1
  N45: TILT1.Pin_1, GPIO_9_|_21.pin1
  3.3V: TILT1.Pin_2, LDR.pin_0, R14.Pin_1, 3v3_|_1.pin1, 3v3_|_17.pin1
  N46: TILT2.Pin_2, GPIO_4_|_7.pin1
  N47: B1.2, GPIO_17_|_11.pin1
  N48: B2.2, GPIO_27_|_13.pin1
  N49: B3.2, GPIO_22_|_15.pin1
  N50: POT.S, R14.Pin_0
  N51: POT.A, C2.+, GPIO_11_|_23.pin1
  N52: LDR.pin_1, C1.+, GPIO_10_|_19.pin1
  N53: SW1.1, GPIO_6_|_31.pin1
  N54: SW1.2, GPIO_5_|_29.pin1
  N55: SW2.2, GPIO_13_|_33.pin1

notes:
  S1
  S2
  S3
  TOP SECRET
  BRONZE THISTLE, General purpose IO test-bed schematic, 1
